// Logisim project ex5.circ as structural Verilog: 1 circuit, main circuit main
module main (
  input  in_1,
  output out_2
);

  wire and_1_out, undriven;

  and and_1 (and_1_out, in_1, undriven);
  not not_1 (out_2, and_1_out);
endmodule
