// Logisim project exercicio13.circ as structural Verilog: 1 circuit, main circuit main
module main (
  input  in_1,
  input  in_2,
  input  in_3,
  output out_4
);

  wire not_1_out;

  not not_1 (not_1_out, in_1);
  buf or_1 (out_4, not_1_out);  // OR_Gate

  assign in_2 = in_1;
  assign in_3 = in_1;
endmodule
